// Logisim project fas32.circ as structural Verilog: 10 circuits, main circuit PG4:进位生成与传递电路
// PG4
module \PG4_进位生成与传递电路  (
  input  [3:0] X,
  input  [3:0] Y,
  output G4,
  output G3,
  output G2,
  output G1,
  output P4,
  output P3,
  output P2,
  output P1
);

  and and_1 (G4, X[3], Y[3]);
  xor xor_1 (P4, X[3], Y[3]);
  and and_2 (G3, X[2], Y[2]);
  xor xor_2 (P3, X[2], Y[2]);
  and and_3 (G2, X[1], Y[1]);
  xor xor_3 (P2, X[1], Y[1]);
  and and_4 (G1, X[0], Y[0]);
  xor xor_4 (P1, X[0], Y[0]);

  // Notes on the sheet:
  //   Y: pull=down
  //   X: pull=down
  //   输入引脚区
  //   PG4：4位生成传递电路
  //   功能说明:根据两组4位输入X和Y，生成相应的Generate信号G1-G4 (Gi = Xi & Yi）和Propagate信号P1-P4（Pi = Xi ^ Yi)
  //   输出引脚区
endmodule

// CLA74182
module \CLA74182_4位先行进位电路  (
  input  G4,
  input  P4,
  input  G3,
  input  P3,
  input  G2,
  input  P2,
  input  G1,
  input  P1,
  input  C0,
  output C4,
  output C3,
  output C2,
  output C1,
  output G_star,
  output P_star
);

  wire and_1_out, and_2_out, and_3_out, and_4_out, and_6_out, and_7_out, and_8_out, and_9_out, and_10_out,
       and_11_out;

  or or_1 (G_star, G4, and_2_out, and_1_out, and_3_out);
  and and_1 (and_1_out, P4, G2, P3);
  and and_2 (and_2_out, P4, G3);
  and and_3 (and_3_out, P3, G1, P4, P2);
  or or_2 (C4, G_star, and_4_out);
  and and_4 (and_4_out, C0, P_star);
  and and_5 (P_star, P4, P3, P2, P1);
  or or_3 (C3, G3, and_6_out, and_7_out, and_8_out);
  and and_6 (and_6_out, G2, P3);
  and and_7 (and_7_out, P3, P2, G1);
  and and_8 (and_8_out, P3, P2, P1, C0);
  or or_4 (C2, G2, and_9_out, and_10_out);
  and and_9 (and_9_out, P2, G1);
  and and_10 (and_10_out, P1, C0, P2);
  or or_5 (C1, G1, and_11_out);
  and and_11 (and_11_out, P1, C0);

  // Notes on the sheet:
  //   P1: pull=down
  //   P2: pull=down
  //   P3: pull=down
  //   G1: pull=down
  //   G2: pull=down
  //   G3: pull=down
  //   G4: pull=down
  //   P4: pull=down
  //   C0: pull=down
  //   CLA74182：4位先行进位电路
  //   输入引脚区
  //   请根据以上引脚以及隧道信号设计完成CLA74182先行进位电路，尽可能使用多输入逻辑门，并分析电路延迟
  //   输出引脚区
endmodule

// FA4
module \FA4_4位快速加法器  (
  input  [3:0] X,
  input  [3:0] Y,
  input  C0,
  output [3:0] S,
  output C4,
  output C3,
  output G_star,
  output P_star
);

  wire \cla74182_4位先行进位电路_1_c1 , \cla74182_4位先行进位电路_1_c2 , \pg4_进位生成与传递电路_1_g1 , \pg4_进位生成与传递电路_1_g2 ,
       \pg4_进位生成与传递电路_1_g3 , \pg4_进位生成与传递电路_1_g4 , \pg4_进位生成与传递电路_1_p1 , \pg4_进位生成与传递电路_1_p2 ,
       \pg4_进位生成与传递电路_1_p3 , \pg4_进位生成与传递电路_1_p4 ;

  \CLA74182_4位先行进位电路  \cla74182_4位先行进位电路_1  (
    .G4(\pg4_进位生成与传递电路_1_g4 ), .P4(\pg4_进位生成与传递电路_1_p4 ), .G3(\pg4_进位生成与传递电路_1_g3 ),
    .P3(\pg4_进位生成与传递电路_1_p3 ), .G2(\pg4_进位生成与传递电路_1_g2 ), .P2(\pg4_进位生成与传递电路_1_p2 ),
    .G1(\pg4_进位生成与传递电路_1_g1 ), .P1(\pg4_进位生成与传递电路_1_p1 ), .C0(C0), .C4(C4), .C3(C3),
    .C2(\cla74182_4位先行进位电路_1_c2 ), .C1(\cla74182_4位先行进位电路_1_c1 ), .G_star(G_star), .P_star(P_star));
  \PG4_进位生成与传递电路  \pg4_进位生成与传递电路_1  (
    .X(X), .Y(Y), .G4(\pg4_进位生成与传递电路_1_g4 ), .G3(\pg4_进位生成与传递电路_1_g3 ), .G2(\pg4_进位生成与传递电路_1_g2 ),
    .G1(\pg4_进位生成与传递电路_1_g1 ), .P4(\pg4_进位生成与传递电路_1_p4 ), .P3(\pg4_进位生成与传递电路_1_p3 ),
    .P2(\pg4_进位生成与传递电路_1_p2 ), .P1(\pg4_进位生成与传递电路_1_p1 ));
  xor xor_1 (S[3], \pg4_进位生成与传递电路_1_p4 , C3);
  xor xor_2 (S[2], \pg4_进位生成与传递电路_1_p3 , \cla74182_4位先行进位电路_1_c2 );
  xor xor_3 (S[1], \pg4_进位生成与传递电路_1_p2 , \cla74182_4位先行进位电路_1_c1 );
  xor xor_4 (S[0], \pg4_进位生成与传递电路_1_p1 , C0);
  // Probe on X
  // Probe on Y
  // Probe on S
  // Probe on X
  // Probe on Y
  // Probe on S

  // Notes on the sheet:
  //   X: pull=down
  //   Y: pull=down
  //   C0: pull=down
  //   输入引脚区
  //   FA4：4位快速加法器
  //   输出引脚区
  //   功能说明:4位Adder  S=X+Y，C4、C3分别为最高和次高进位，C0为进位输入， G* P*为成组进位生成传递函数
  //   +
  //   =
  //   有符号加法
  //   +
  //   =
  //   无符号加法
endmodule

// FA16
module \FA16_16位快速加法器  (
  input  [15:0] X,
  input  [15:0] Y,
  input  C0,
  output C16,
  output C15,
  output G_star,
  output P_star,
  output [15:0] S
);

  wire \cla74182_4位先行进位电路_1_c1 , \cla74182_4位先行进位电路_1_c2 , \cla74182_4位先行进位电路_1_c3 , \fa4_4位快速加法器_1_g_star ,
       \fa4_4位快速加法器_1_p_star , \fa4_4位快速加法器_2_g_star , \fa4_4位快速加法器_2_p_star , \fa4_4位快速加法器_3_g_star ,
       \fa4_4位快速加法器_3_p_star , \fa4_4位快速加法器_4_g_star , \fa4_4位快速加法器_4_p_star ;

  \CLA74182_4位先行进位电路  \cla74182_4位先行进位电路_1  (
    .G4(\fa4_4位快速加法器_1_g_star ), .P4(\fa4_4位快速加法器_1_p_star ), .G3(\fa4_4位快速加法器_2_g_star ),
    .P3(\fa4_4位快速加法器_2_p_star ), .G2(\fa4_4位快速加法器_3_g_star ), .P2(\fa4_4位快速加法器_3_p_star ),
    .G1(\fa4_4位快速加法器_4_g_star ), .P1(\fa4_4位快速加法器_4_p_star ), .C0(C0), .C4(C16),
    .C3(\cla74182_4位先行进位电路_1_c3 ), .C2(\cla74182_4位先行进位电路_1_c2 ), .C1(\cla74182_4位先行进位电路_1_c1 ),
    .G_star(G_star), .P_star(P_star));
  \FA4_4位快速加法器  \fa4_4位快速加法器_1  (
    .X(X[15:12]), .Y(Y[15:12]), .C0(\cla74182_4位先行进位电路_1_c3 ), .S(S[15:12]), .G_star(\fa4_4位快速加法器_1_g_star ),
    .P_star(\fa4_4位快速加法器_1_p_star ), .C3(C15));  // open: C4
  \FA4_4位快速加法器  \fa4_4位快速加法器_2  (
    .X(X[11:8]), .Y(Y[11:8]), .C0(\cla74182_4位先行进位电路_1_c2 ), .S(S[11:8]), .G_star(\fa4_4位快速加法器_2_g_star ),
    .P_star(\fa4_4位快速加法器_2_p_star ));  // open: C4, C3
  \FA4_4位快速加法器  \fa4_4位快速加法器_3  (
    .X(X[7:4]), .Y(Y[7:4]), .C0(\cla74182_4位先行进位电路_1_c1 ), .S(S[7:4]), .G_star(\fa4_4位快速加法器_3_g_star ),
    .P_star(\fa4_4位快速加法器_3_p_star ));  // open: C4, C3
  // Probe on X
  // Probe on Y
  // Probe on C0
  // Probe on S
  \FA4_4位快速加法器  \fa4_4位快速加法器_4  (
    .X(X[3:0]), .Y(Y[3:0]), .C0(C0), .S(S[3:0]), .G_star(\fa4_4位快速加法器_4_g_star ),
    .P_star(\fa4_4位快速加法器_4_p_star ));  // open: C4, C3
  // Probe on X
  // Probe on Y
  // Probe on C0
  // Probe on S

  // Other names for the same wires on the sheet: S0[3:0] = S[3:0]; S1[3:0] = S[7:4]; S2[3:0] = S[11:8];
  //   S3[3:0] = S[15:12]; X0[3:0] = X[3:0]; X1[3:0] = X[7:4]; X2[3:0] = X[11:8]; X3[3:0] = X[15:12]; Y0[3:0] = Y[3:0];
  //   Y1[3:0] = Y[7:4]; Y2[3:0] = Y[11:8]; Y3[3:0] = Y[15:12]

  // Notes on the sheet:
  //   C0: pull=down
  //   X: pull=down
  //   Y: pull=down
  //   输入引脚区
  //   FA16：16位快速加法器
  //   输出引脚区
  //   功能说明：16位Adder  S=X＋Y，C16、C15分别为最高和次高进位，C0为进位输入， G* P*为成组进位生成传递函数
  //   +
  //   =
  //   有符号加法
  //   +
  //   =
  //   无符号加法
endmodule

// FA32
module \FA32_32位快速加法器  (
  input  C0,
  input  [31:0] X,
  input  [31:0] Y,
  output C32,
  output C31,
  output [31:0] S
);

  wire \cla74182_4位先行进位电路_1_c1 , \cla74182_4位先行进位电路_1_c2 , \cla74182_4位先行进位电路_1_c3 ,
       \cla74182_4位先行进位电路_2_c1 , \cla74182_4位先行进位电路_2_c2 , \cla74182_4位先行进位电路_2_c3 , \fa4_4位快速加法器_1_g_star ,
       \fa4_4位快速加法器_1_p_star , \fa4_4位快速加法器_2_g_star , \fa4_4位快速加法器_2_p_star , \fa4_4位快速加法器_3_g_star ,
       \fa4_4位快速加法器_3_p_star , \fa4_4位快速加法器_4_g_star , \fa4_4位快速加法器_4_p_star , \fa4_4位快速加法器_5_c4 ,
       \fa4_4位快速加法器_5_g_star , \fa4_4位快速加法器_5_p_star , \fa4_4位快速加法器_6_g_star , \fa4_4位快速加法器_6_p_star ,
       \fa4_4位快速加法器_7_g_star , \fa4_4位快速加法器_7_p_star , \fa4_4位快速加法器_8_g_star , \fa4_4位快速加法器_8_p_star ;

  \CLA74182_4位先行进位电路  \cla74182_4位先行进位电路_1  (
    .G4(\fa4_4位快速加法器_1_g_star ), .P4(\fa4_4位快速加法器_1_p_star ), .G3(\fa4_4位快速加法器_2_g_star ),
    .P3(\fa4_4位快速加法器_2_p_star ), .G2(\fa4_4位快速加法器_3_g_star ), .P2(\fa4_4位快速加法器_3_p_star ),
    .G1(\fa4_4位快速加法器_4_g_star ), .P1(\fa4_4位快速加法器_4_p_star ), .C0(\fa4_4位快速加法器_5_c4 ), .C4(C32),
    .C3(\cla74182_4位先行进位电路_1_c3 ), .C2(\cla74182_4位先行进位电路_1_c2 ), .C1(\cla74182_4位先行进位电路_1_c1 ));  // open: G_star, P_star
  \FA4_4位快速加法器  \fa4_4位快速加法器_1  (
    .X(X[31:28]), .Y(Y[31:28]), .C0(\cla74182_4位先行进位电路_1_c3 ), .S(S[31:28]), .G_star(\fa4_4位快速加法器_1_g_star ),
    .P_star(\fa4_4位快速加法器_1_p_star ), .C3(C31));  // open: C4
  \FA4_4位快速加法器  \fa4_4位快速加法器_2  (
    .X(X[27:24]), .Y(Y[27:24]), .C0(\cla74182_4位先行进位电路_1_c2 ), .S(S[27:24]), .G_star(\fa4_4位快速加法器_2_g_star ),
    .P_star(\fa4_4位快速加法器_2_p_star ));  // open: C4, C3
  \FA4_4位快速加法器  \fa4_4位快速加法器_3  (
    .X(X[23:20]), .Y(Y[23:20]), .C0(\cla74182_4位先行进位电路_1_c1 ), .S(S[23:20]), .G_star(\fa4_4位快速加法器_3_g_star ),
    .P_star(\fa4_4位快速加法器_3_p_star ));  // open: C4, C3
  // Probe on X
  // Probe on Y
  // Probe on C0
  // Probe on S
  \FA4_4位快速加法器  \fa4_4位快速加法器_4  (
    .X(X[19:16]), .Y(Y[19:16]), .C0(\fa4_4位快速加法器_5_c4 ), .S(S[19:16]), .G_star(\fa4_4位快速加法器_4_g_star ),
    .P_star(\fa4_4位快速加法器_4_p_star ));  // open: C4, C3
  \CLA74182_4位先行进位电路  \cla74182_4位先行进位电路_2  (
    .G4(\fa4_4位快速加法器_5_g_star ), .P4(\fa4_4位快速加法器_5_p_star ), .G3(\fa4_4位快速加法器_6_g_star ),
    .P3(\fa4_4位快速加法器_6_p_star ), .G2(\fa4_4位快速加法器_7_g_star ), .P2(\fa4_4位快速加法器_7_p_star ),
    .G1(\fa4_4位快速加法器_8_g_star ), .P1(\fa4_4位快速加法器_8_p_star ), .C0(C0), .C3(\cla74182_4位先行进位电路_2_c3 ),
    .C2(\cla74182_4位先行进位电路_2_c2 ), .C1(\cla74182_4位先行进位电路_2_c1 ));  // open: C4, G_star, P_star
  // Probe on X
  // Probe on Y
  // Probe on C0
  // Probe on S
  \FA4_4位快速加法器  \fa4_4位快速加法器_5  (
    .X(X[15:12]), .Y(Y[15:12]), .C0(\cla74182_4位先行进位电路_2_c3 ), .S(S[15:12]), .C4(\fa4_4位快速加法器_5_c4 ),
    .G_star(\fa4_4位快速加法器_5_g_star ), .P_star(\fa4_4位快速加法器_5_p_star ));  // open: C3
  \FA4_4位快速加法器  \fa4_4位快速加法器_6  (
    .X(X[11:8]), .Y(Y[11:8]), .C0(\cla74182_4位先行进位电路_2_c2 ), .S(S[11:8]), .G_star(\fa4_4位快速加法器_6_g_star ),
    .P_star(\fa4_4位快速加法器_6_p_star ));  // open: C4, C3
  \FA4_4位快速加法器  \fa4_4位快速加法器_7  (
    .X(X[7:4]), .Y(Y[7:4]), .C0(\cla74182_4位先行进位电路_2_c1 ), .S(S[7:4]), .G_star(\fa4_4位快速加法器_7_g_star ),
    .P_star(\fa4_4位快速加法器_7_p_star ));  // open: C4, C3
  \FA4_4位快速加法器  \fa4_4位快速加法器_8  (
    .X(X[3:0]), .Y(Y[3:0]), .C0(C0), .S(S[3:0]), .G_star(\fa4_4位快速加法器_8_g_star ),
    .P_star(\fa4_4位快速加法器_8_p_star ));  // open: C4, C3

  // Other names for the same wires on the sheet: S0[3:0] = S[3:0]; S1[3:0] = S[7:4]; S2[3:0] = S[11:8];
  //   S3[3:0] = S[15:12]; S4[3:0] = S[19:16]; S5[3:0] = S[23:20]; S6[3:0] = S[27:24]; S7[3:0] = S[31:28];
  //   X0[3:0] = X[3:0]; X1[3:0] = X[7:4]; X2[3:0] = X[11:8]; X3[3:0] = X[15:12]; X4[3:0] = X[19:16];
  //   X5[3:0] = X[23:20]; X6[3:0] = X[27:24]; X7[3:0] = X[31:28]; Y0[3:0] = Y[3:0]; Y1[3:0] = Y[7:4];
  //   Y2[3:0] = Y[11:8]; Y3[3:0] = Y[15:12]; Y4[3:0] = Y[19:16]; Y5[3:0] = Y[23:20]; Y6[3:0] = Y[27:24];
  //   Y7[3:0] = Y[31:28]

  // Notes on the sheet:
  //   X: pull=down
  //   Y: pull=down
  //   C0: pull=down
  //   输入引脚区
  //   FA32：32位快速加法器
  //   输出引脚区
  //   功能说明：利用已完成的74182以及4位快速加法器构建快速32位加法器 S = X ＋ Y，并分析电路延迟；
  //   +
  //   =
  //   有符号加法
  //   +
  //   =
  //   无符号加法
  //   C32、C31分别为最高和次高进位，C0为进位输入
endmodule

module \FAS32_32位快速加减法器  (
  input  Sub,
  input  [31:0] X,
  input  [31:0] Y,
  output OF,
  output UOF,
  output [31:0] S
);

  wire \cla74182_4位先行进位电路_1_c1 , \cla74182_4位先行进位电路_1_c2 , \cla74182_4位先行进位电路_1_c3 ,
       \cla74182_4位先行进位电路_1_c4 , \cla74182_4位先行进位电路_2_c1 , \cla74182_4位先行进位电路_2_c2 ,
       \cla74182_4位先行进位电路_2_c3 , \fa4_4位快速加法器_1_c3 , \fa4_4位快速加法器_1_c4 , \fa4_4位快速加法器_1_g_star ,
       \fa4_4位快速加法器_1_p_star , \fa4_4位快速加法器_2_g_star , \fa4_4位快速加法器_2_p_star , \fa4_4位快速加法器_3_g_star ,
       \fa4_4位快速加法器_3_p_star , \fa4_4位快速加法器_4_g_star , \fa4_4位快速加法器_4_p_star , \fa4_4位快速加法器_5_c4 ,
       \fa4_4位快速加法器_5_g_star , \fa4_4位快速加法器_5_p_star , \fa4_4位快速加法器_6_g_star , \fa4_4位快速加法器_6_p_star ,
       \fa4_4位快速加法器_7_g_star , \fa4_4位快速加法器_7_p_star , \fa4_4位快速加法器_8_g_star , \fa4_4位快速加法器_8_p_star ;
  wire [3:0] bit_extender_1_out, xor_3_out, xor_4_out, xor_5_out, xor_6_out, xor_7_out, xor_8_out, xor_9_out,
       xor_10_out;

  xor xor_1 (UOF, Sub, \cla74182_4位先行进位电路_1_c4 );
  xor xor_2 (OF, \fa4_4位快速加法器_1_c4 , \fa4_4位快速加法器_1_c3 );
  \CLA74182_4位先行进位电路  \cla74182_4位先行进位电路_1  (
    .G4(\fa4_4位快速加法器_1_g_star ), .P4(\fa4_4位快速加法器_1_p_star ), .G3(\fa4_4位快速加法器_2_g_star ),
    .P3(\fa4_4位快速加法器_2_p_star ), .G2(\fa4_4位快速加法器_3_g_star ), .P2(\fa4_4位快速加法器_3_p_star ),
    .G1(\fa4_4位快速加法器_4_g_star ), .P1(\fa4_4位快速加法器_4_p_star ), .C0(\fa4_4位快速加法器_5_c4 ),
    .C4(\cla74182_4位先行进位电路_1_c4 ), .C3(\cla74182_4位先行进位电路_1_c3 ), .C2(\cla74182_4位先行进位电路_1_c2 ),
    .C1(\cla74182_4位先行进位电路_1_c1 ));  // open: G_star, P_star
  \FA4_4位快速加法器  \fa4_4位快速加法器_1  (
    .X(X[31:28]), .Y(xor_3_out), .C0(\cla74182_4位先行进位电路_1_c3 ), .S(S[31:28]), .C4(\fa4_4位快速加法器_1_c4 ),
    .G_star(\fa4_4位快速加法器_1_g_star ), .P_star(\fa4_4位快速加法器_1_p_star ), .C3(\fa4_4位快速加法器_1_c3 ));
  assign xor_3_out = Y[31:28] ^ bit_extender_1_out;  // XOR_Gate xor_3, 4 bits wide
  \FA4_4位快速加法器  \fa4_4位快速加法器_2  (
    .X(X[27:24]), .Y(xor_4_out), .C0(\cla74182_4位先行进位电路_1_c2 ), .S(S[27:24]),
    .G_star(\fa4_4位快速加法器_2_g_star ), .P_star(\fa4_4位快速加法器_2_p_star ));  // open: C4, C3
  assign xor_4_out = Y[27:24] ^ bit_extender_1_out;  // XOR_Gate xor_4, 4 bits wide
  \FA4_4位快速加法器  \fa4_4位快速加法器_3  (
    .X(X[23:20]), .Y(xor_5_out), .C0(\cla74182_4位先行进位电路_1_c1 ), .S(S[23:20]),
    .G_star(\fa4_4位快速加法器_3_g_star ), .P_star(\fa4_4位快速加法器_3_p_star ));  // open: C4, C3
  assign xor_5_out = Y[23:20] ^ bit_extender_1_out;  // XOR_Gate xor_5, 4 bits wide
  assign xor_6_out = Y[19:16] ^ bit_extender_1_out;  // XOR_Gate xor_6, 4 bits wide
  // Probe on X
  // Probe on Y
  // Probe on S
  \FA4_4位快速加法器  \fa4_4位快速加法器_4  (
    .X(X[19:16]), .Y(xor_6_out), .C0(\fa4_4位快速加法器_5_c4 ), .S(S[19:16]), .G_star(\fa4_4位快速加法器_4_g_star ),
    .P_star(\fa4_4位快速加法器_4_p_star ));  // open: C4, C3
  \CLA74182_4位先行进位电路  \cla74182_4位先行进位电路_2  (
    .G4(\fa4_4位快速加法器_5_g_star ), .P4(\fa4_4位快速加法器_5_p_star ), .G3(\fa4_4位快速加法器_6_g_star ),
    .P3(\fa4_4位快速加法器_6_p_star ), .G2(\fa4_4位快速加法器_7_g_star ), .P2(\fa4_4位快速加法器_7_p_star ),
    .G1(\fa4_4位快速加法器_8_g_star ), .P1(\fa4_4位快速加法器_8_p_star ), .C0(Sub), .C3(\cla74182_4位先行进位电路_2_c3 ),
    .C2(\cla74182_4位先行进位电路_2_c2 ), .C1(\cla74182_4位先行进位电路_2_c1 ));  // open: C4, G_star, P_star
  assign xor_7_out = Y[15:12] ^ bit_extender_1_out;  // XOR_Gate xor_7, 4 bits wide
  // Probe on X
  // Probe on Y
  // Probe on S
  \FA4_4位快速加法器  \fa4_4位快速加法器_5  (
    .X(X[15:12]), .Y(xor_7_out), .C0(\cla74182_4位先行进位电路_2_c3 ), .S(S[15:12]), .C4(\fa4_4位快速加法器_5_c4 ),
    .G_star(\fa4_4位快速加法器_5_g_star ), .P_star(\fa4_4位快速加法器_5_p_star ));  // open: C3
  \FA4_4位快速加法器  \fa4_4位快速加法器_6  (
    .X(X[11:8]), .Y(xor_8_out), .C0(\cla74182_4位先行进位电路_2_c2 ), .S(S[11:8]), .G_star(\fa4_4位快速加法器_6_g_star ),
    .P_star(\fa4_4位快速加法器_6_p_star ));  // open: C4, C3
  assign xor_8_out = Y[11:8] ^ bit_extender_1_out;  // XOR_Gate xor_8, 4 bits wide
  \FA4_4位快速加法器  \fa4_4位快速加法器_7  (
    .X(X[7:4]), .Y(xor_9_out), .C0(\cla74182_4位先行进位电路_2_c1 ), .S(S[7:4]), .G_star(\fa4_4位快速加法器_7_g_star ),
    .P_star(\fa4_4位快速加法器_7_p_star ));  // open: C4, C3
  assign xor_9_out = Y[7:4] ^ bit_extender_1_out;  // XOR_Gate xor_9, 4 bits wide
  \FA4_4位快速加法器  \fa4_4位快速加法器_8  (
    .X(X[3:0]), .Y(xor_10_out), .C0(Sub), .S(S[3:0]), .G_star(\fa4_4位快速加法器_8_g_star ),
    .P_star(\fa4_4位快速加法器_8_p_star ));  // open: C4, C3
  assign xor_10_out = Y[3:0] ^ bit_extender_1_out;  // XOR_Gate xor_10, 4 bits wide
  assign bit_extender_1_out = {{3{Sub}}, Sub};  // Bit_Extender bit_extender_1

  // Other names for the same wires on the sheet: S0[3:0] = S[3:0]; S1[3:0] = S[7:4]; S2[3:0] = S[11:8];
  //   S3[3:0] = S[15:12]; S4[3:0] = S[19:16]; S5[3:0] = S[23:20]; S6[3:0] = S[27:24]; S7[3:0] = S[31:28];
  //   X0[3:0] = X[3:0]; X1[3:0] = X[7:4]; X2[3:0] = X[11:8]; X3[3:0] = X[15:12]; X4[3:0] = X[19:16];
  //   X5[3:0] = X[23:20]; X6[3:0] = X[27:24]; X7[3:0] = X[31:28]; Y0[3:0] = Y[3:0]; Y1[3:0] = Y[7:4];
  //   Y2[3:0] = Y[11:8]; Y3[3:0] = Y[15:12]; Y4[3:0] = Y[19:16]; Y5[3:0] = Y[23:20]; Y6[3:0] = Y[27:24];
  //   Y7[3:0] = Y[31:28]

  // Notes on the sheet:
  //   X: pull=down
  //   Y: pull=down
  //   Sub: pull=down
  //   输入引脚区
  //   FA32S：32位快速加减法器
  //   输出引脚区
  //   功能说明：以FA32为基础，实现加减法器FAS32。其中Sub=1做减法，Sub=0做加法。注意：FAS32无进位输入C0。
  //   +/-
  //   =
  //   有符号加减法
  //   +/-
  //   =
  //   无符号加减法
  //   OF/UOF分别为有符号和无符号溢出信号。
endmodule

// FA
module \一位全加器FA封装1  (
  input  Cin,
  input  Xi,
  input  Yi,
  output Cout,
  output Si
);

  wire AND_2_out, AND_out, XOR_2_out;

  or OR (Cout, AND_out, AND_2_out);
  and AND (AND_out, Xi, Yi);
  and AND_2 (AND_2_out, Cin, XOR_2_out);
  xor XOR (Si, Cin, XOR_2_out);
  xor XOR_2 (XOR_2_out, Xi, Yi);

  // Notes on the sheet:
  //   Yi: pull=down
  //   Cin: pull=down
  //   Xi: pull=down
  //   Si = Xi ^ Yi ^ Cin
  //   Cout = Xi Yi + Cin (Xi ^ Yi)
endmodule

module \一位全加器FA封装3  (
  input  Cin,
  input  Xi,
  input  Yi,
  output Cout,
  output Si
);

  wire AND_2_out, AND_out, XOR_2_out;

  or OR (Cout, AND_out, AND_2_out);
  and AND (AND_out, Xi, Yi);
  and AND_2 (AND_2_out, Cin, XOR_2_out);
  xor XOR (Si, Cin, XOR_2_out);
  xor XOR_2 (XOR_2_out, Xi, Yi);

  // Notes on the sheet:
  //   Si = Xi ^ Yi ^ Cin
  //   Cout = Xi Yi + Cin (Xi ^ Yi)
endmodule

// Trace
module trace (
  input  [7:0] in_1,
  output [31:0] X,
  output [31:0] Y,
  output [31:0] R,
  output [31:0] R2,
  output [2:0] FLAGS
);

  ROM #(.addrWidth(8), .dataWidth(32), .Select("high")) rom_1 (.addr(in_1), .data(X));
  ROM #(.addrWidth(8), .dataWidth(32), .Select("high")) rom_2 (.addr(in_1), .data(Y));
  ROM #(.addrWidth(8), .dataWidth(32), .Select("high")) rom_3 (.addr(in_1), .data(R));
  ROM #(.addrWidth(8), .dataWidth(32), .Select("high")) rom_4 (.addr(in_1), .data(R2));
  ROM #(.addrWidth(8), .dataWidth(3), .Select("high")) rom_5 (.addr(in_1), .data(FLAGS));

  // Notes on the sheet:
  //   X trace
  //   Y trace
  //   Result
  //   Result2 Benchmark
  //   FLAGS Benchmark
  //   contents of rom_1 (hex, n*v repeats v):
  //   ff00ffff ff00ffff ff000000 ff00ffff 7fffffff fffffffe ffff ffffffff 7fffffff 80000000 7ff00000 7c
  //   80000000 7fffffff ff00ffff 7fffffff 18*fffffffe
  //   contents of rom_2 (hex, n*v repeats v):
  //   7 ff00ffff 18 18 10 10 80 ffffffff c 80000000 7c 7ff00000 1 fffffffe 18 74 fffffffe 88 10 ffffffff
  //   10 ffffffff 12*10
  //   contents of rom_3 (hex, n*v repeats v):
  //   807fff80 80000000 ffffffff ff fffffff0 fffffff 1007f fffffffe 8000000b 0 7fefff84 8010007c 7fffffff
  //   80000001 18 7fffffff 0 1 1 1 0 1 300000 11*ffffffee 1
  //   contents of rom_4 (hex, n*v repeats v):
  //   4*0 7 e
  //   contents of rom_5 (hex, n*v repeats v):
  //   0 1 5*0 3 4 7 0 2 4 6 0 0 1 17*0 66*1
endmodule

module sub (
  input  in_1,
  input  [3:0] in_2,
  output [3:0] out
);

  wire [3:0] bit_extender_1_out;

  assign out = in_2 ^ bit_extender_1_out;  // XOR_Gate xor_1, 4 bits wide
  assign bit_extender_1_out = {{3{in_1}}, in_1};  // Bit_Extender bit_extender_1
endmodule
